# Fritzing sketch serial_Kg7cU9ssU3 (saved by Fritzing 0.9.2b)
breadboards: 1

parts:
  Part1 = Arduino Uno (Rev3)
  Part2 = Spark Core (v1.0)

nets:
  N1: Part1.D0/RX, Part2.TX
  N2: Part1.D1/TX, Part2.RX
  5V: Part1.5V, Part2.VIN
  GND: Part1.GND, Part2.GND
